# Fritzing sketch Arossage auto plantes copie (saved by Fritzing 1.0.2b)
breadboards: 1

parts:
  Composant1 = Arduino Uno (Rev3)
  Q1 = TRANSISTOR_NPN [package=to-92-ammo]
  R1 = Resistor [tolerance=±5% resistance=220 package="0805 [SMD]"]
  R2 = Resistor [tolerance=±5% resistance=33 power=0.25W package=THT]
  Composant4 = Soil Moisture Sensor  # not connected
  U2 = Vibration Motor- ROB-08449 [package=vibe-motor-10mm]
  M1 = DC Motor [voltage_(max)=6V voltage_(min)=3V part_number=5V]
  LED2 = smd LED [color="Red (633nm)" package="1206 [SMD]"]
  SP1 = SPEAKER [package=pcb_mount_speaker]
  LTR_1 = Monacor line transformer [part_number=LTR-110]
  Composant5 = Soil Moisture Sensor  # not connected
  LED3 = LED - 5mm [color="Green (570nm)" current=0.030A package="5 mm [THT]"]
  R4 = Resistor [tolerance=±5% power=0.25W resistance=150 package=THT]
  ZS-042_RTC1 = ZS-042 RTC Module
  U3 = LCD-16X2 [package=lcd-8x2-kit]
  S1 = Pushbutton [package="[THT]"]
  R5 = Resistor [tolerance=±5% resistance=1k package="2512 [SMD]"]

nets:
  N1: Composant1.A4/SDA, ZS-042_RTC1.SDA, U3.A
  N2: Composant1.A5/SCL, ZS-042_RTC1.SCL, U3.DB6
  N3: Composant1.D8, R2.Pin_0
  N4: Composant1.D10_PWM/SS, R4.Pin_1
  N5: Composant1.D12/MISO, LED2.anode
  GND: Composant1.GND, Q1.E, R1.Pin_1, U2.+, LED3.cathode, ZS-042_RTC1.GND, U3.DB7, R5.Pin_1
  N6: Composant1.D2, SP1.-
  N7: Composant1.D3_PWM, S1.Pin_1, S1.Pin_2, R5.Pin_0
  N8: Composant1.3V3, U3.K
  N9: Composant1.5V, U2.-, S1.Pin_3, S1.Pin_4
  VIN: Composant1.VIN, ZS-042_RTC1.VCC
  N10: Q1.B, R2.Pin_1
  N11: R1.Pin_0, LED2.cathode
  N12: M1.pin_2, LTR_1.GND

notes:
  POMPE À EAU
  CAPTEUR D'HUMIDITÉ ( LM393 ) DANS LA TERRE
  ←CAPTEUR D'EAU EXTERNE (Model: XKC-Y25-NPN)
  HAUT PARLEUR
  ← ALIMENTATION 5V DC
  LED VERTE = EN FONCTION
  LED ROUGE = MANQUE D'EAU OU PLATEAU PLEIN
  5 V
  ←ALIMENTATION 110V AC
  TUYAU POUR L'EAU
  RELAIS 5 V
  VCC
  GND
  →  →  →
  - NOTE -
  ← BC 547 (NPN)
  CAPTEUR D'HUMIDITÉ ( LM393 ) DANS LE PLATEAU
  Module RTC: DS1307
  SDA
  SCL
  ÉCRAN LCD
  ↙︎ Activation Manuel
